// Logisim project CIs.circ as structural Verilog: 10 circuits, main circuit main
module main (
  input  nEN,
  input  I3,
  input  I2,
  input  I1,
  input  I0,
  input  A,
  input  B,
  output I3_2,
  output I2_2,
  output I1_2,
  output I0_2
);

  wire mux_4_1_1_out_8;

  MUX_4_1 mux_4_1_1 (.I3(I3), .I2(I2), .I1(I1), .I0(I0), .B(B), .A(A), .EN(nEN), .out_8(mux_4_1_1_out_8));
  DMUX_1_4 dmux_1_4_1 (.EN(nEN), .D(mux_4_1_1_out_8), .B(B), .A(A), .Y3(I3_2), .Y2(I2_2), .Y1(I1_2), .Y0(I0_2));
endmodule

module _2_4_Decoder (
  input  I0,
  input  I1,
  input  EN,
  output Y0,
  output Y1,
  output Y2,
  output Y3
);

  wire not_1_out, not_2_out;

  not not_1 (not_1_out, I0);
  not not_2 (not_2_out, I1);
  and and_1 (Y0, not_2_out, not_1_out, EN);
  and and_2 (Y1, I0, not_2_out, EN);
  and and_3 (Y2, I1, not_1_out, EN);
  and and_4 (Y3, I0, I1, EN);
endmodule

module _3_8_Decoder (
  input  G1,
  input  G2A,
  input  G2B,
  input  A,
  input  B,
  input  C,
  input  C_2,
  input  EN,
  input  B_2,
  input  A_2,
  output Y7,
  output Y0,
  output Y1,
  output Y6,
  output Y2,
  output Y5,
  output Y3,
  output Y4,
  output Y4_2,
  output Y5_2,
  output Y3_2,
  output Y6_2,
  output Y7_2,
  output Y2_2,
  output Y1_2,
  output Y0_2
);

  wire and_1_out, and_2_out, and_3_out, not_1_out, not_2_out, not_3_out, not_4_out, not_5_out, not_6_out;

  not not_1 (not_1_out, G2A);
  not not_2 (not_2_out, G2B);
  and and_1 (and_1_out, G1, not_1_out, not_2_out);
  not not_3 (not_3_out, C_2);
  not not_4 (not_4_out, B_2);
  not not_5 (not_5_out, A_2);
  nand nand_1 (Y7, and_1_out, C_2, B_2, A_2);
  nand nand_2 (Y6, and_1_out, C_2, B_2, not_5_out);
  nand nand_3 (Y5, and_1_out, C_2, not_4_out, A_2);
  nand nand_4 (Y4_2, and_1_out, not_5_out, C_2, not_4_out);
  nand nand_5 (Y3_2, and_1_out, B_2, A_2, not_3_out);
  nand nand_6 (Y2_2, and_1_out, B_2, not_3_out, not_5_out);
  nand nand_7 (Y1_2, and_1_out, not_4_out, not_3_out, A_2);
  nand nand_8 (Y0_2, and_1_out, not_5_out, not_4_out, not_3_out);
  not not_6 (not_6_out, C);
  and and_2 (and_2_out, not_6_out, EN);
  and and_3 (and_3_out, C, EN);
  _2_4_Decoder u_2_4_decoder_1 (.I0(A), .I1(B), .EN(and_2_out), .Y0(Y0), .Y1(Y1), .Y2(Y2), .Y3(Y3));
  _2_4_Decoder u_2_4_decoder_2 (.I0(A), .I1(B), .EN(and_3_out), .Y0(Y4), .Y1(Y5_2), .Y2(Y6_2), .Y3(Y7_2));
endmodule

module MUX_4_1 (
  input  I3,
  input  I2,
  input  I1,
  input  I0,
  input  B,
  input  A,
  input  EN,
  output out_8
);

  wire and_1_out, and_2_out, and_3_out, and_4_out, not_1_out, not_2_out, not_3_out;

  not not_1 (not_1_out, B);
  not not_2 (not_2_out, A);
  not not_3 (not_3_out, EN);
  and and_1 (and_1_out, I3, B, A, not_3_out);
  and and_2 (and_2_out, I2, B, not_2_out, not_3_out);
  and and_3 (and_3_out, I1, not_1_out, A, not_3_out);
  and and_4 (and_4_out, I0, not_1_out, not_2_out, not_3_out);
  or or_1 (out_8, and_1_out, and_2_out, and_3_out, and_4_out);
endmodule

module _8_3_Encoder (
  input  Y7,
  input  Y6,
  input  Y5,
  input  Y4,
  input  Y3,
  input  Y2,
  input  Y1,
  input  Y0,
  output I2,
  output I1,
  output I0
);

  or or_1 (I2, Y7, Y6, Y5, Y4);
  or or_2 (I1, Y7, Y6, Y3, Y2);
  or or_3 (I0, Y7, Y5, Y3, Y1);
endmodule

module MUX_8_1 (
  input  Y7,
  input  Y6,
  input  Y5,
  input  Y4,
  input  Y3,
  input  Y2,
  input  Y1,
  input  I7,
  input  I6,
  input  I5,
  input  Y0,
  input  I4,
  input  C,
  input  nEN,
  input  A,
  input  B,
  input  B_2,
  input  A_2,
  input  I3,
  input  I2,
  input  EN,
  input  I1,
  input  I0,
  input  C_2,
  output Y,
  output nY,
  output OUT
);

  wire and_1_out, and_2_out, and_3_out, and_4_out, and_5_out, and_6_out, and_7_out, and_8_out,
       mux_4_1_1_out_8, mux_4_1_2_out_8, not_1_out, not_2_out, not_3_out, not_4_out, not_6_out;

  not not_1 (not_1_out, EN);
  not not_2 (not_2_out, C);
  not not_3 (not_3_out, B_2);
  not not_4 (not_4_out, A_2);
  and and_1 (and_1_out, Y7, C, B_2, A_2, not_1_out);
  and and_2 (and_2_out, Y6, C, B_2, not_4_out, not_1_out);
  and and_3 (and_3_out, Y5, C, not_3_out, A_2, not_1_out);
  and and_4 (and_4_out, Y4, C, not_3_out, not_4_out, not_1_out);
  and and_5 (and_5_out, Y3, not_2_out, B_2, A_2, not_1_out);
  and and_6 (and_6_out, Y2, not_2_out, B_2, not_4_out, not_1_out);
  and and_7 (and_7_out, Y1, not_2_out, not_3_out, A_2, not_1_out);
  and and_8 (and_8_out, Y0, not_2_out, not_3_out, not_4_out, not_1_out);
  nor nor_1 (nY, and_1_out, and_2_out, and_3_out, and_4_out, and_5_out, and_6_out, and_7_out, and_8_out);
  not not_5 (Y, nY);
  MUX_4_1 mux_4_1_1 (.I3(I7), .I2(I6), .I1(I5), .I0(I4), .B(B), .A(A), .EN(nEN), .out_8(mux_4_1_1_out_8));
  MUX_4_1 mux_4_1_2 (.I3(I3), .I2(I2), .I1(I1), .I0(I0), .B(B), .A(A), .EN(nEN), .out_8(mux_4_1_2_out_8));
  not not_6 (not_6_out, nEN);
  Multiplexer multiplexer_1 (.in0(mux_4_1_2_out_8), .in1(mux_4_1_1_out_8), .out(OUT), .sel(C_2), .en(not_6_out));
endmodule

module DMUX_1_8 (
  input  EN,
  input  F,
  input  C,
  input  B,
  input  A,
  output Y7,
  output Y6,
  output Y5,
  output Y4,
  output Y3,
  output Y2,
  output Y1,
  output Y0
);

  wire not_1_out, not_2_out, not_3_out, not_4_out;

  not not_1 (not_1_out, EN);
  not not_2 (not_2_out, C);
  not not_3 (not_3_out, B);
  not not_4 (not_4_out, A);
  and and_1 (Y7, F, C, not_1_out, B, A);
  and and_2 (Y6, F, C, not_1_out, B, not_4_out);
  and and_3 (Y5, F, C, not_1_out, not_3_out, A);
  and and_4 (Y4, F, C, not_1_out, not_3_out, not_4_out);
  and and_5 (Y3, F, not_2_out, not_1_out, B, A);
  and and_6 (Y2, F, not_2_out, not_1_out, B, not_4_out);
  and and_7 (Y1, F, not_2_out, not_1_out, not_3_out, A);
  and and_8 (Y0, F, not_3_out, not_4_out, not_2_out);
endmodule

module DMUX_1_4 (
  input  EN,
  input  D,
  input  B,
  input  A,
  output Y3,
  output Y2,
  output Y1,
  output Y0
);

  wire not_1_out, not_2_out, not_3_out;

  not not_1 (not_1_out, EN);
  not not_2 (not_2_out, B);
  not not_3 (not_3_out, A);
  and and_1 (Y3, not_1_out, D, B, A);
  and and_2 (Y2, not_1_out, D, B, not_3_out);
  and and_3 (Y1, not_1_out, D, not_2_out, A);
  and and_4 (Y0, not_1_out, D, not_2_out, not_3_out);
endmodule

module _4_2_Encoder (
  input  A3,
  input  A2,
  input  A1,
  input  A0,
  output F0,
  output F1
);

  or or_1 (F0, A3, A1);
  or or_2 (F1, A3, A2);
endmodule

module _4_16_Decoder (
  input  I2,
  input  I3,
  input  EN,
  input  I0,
  input  I1,
  output Y0,
  output Y1,
  output Y2,
  output Y3,
  output Y4,
  output Y5,
  output Y6,
  output Y7,
  output Y8,
  output Y9,
  output Y10,
  output Y11,
  output Y12,
  output Y13,
  output Y14,
  output Y15
);

  wire n2_4_decoder_1_y0, n2_4_decoder_1_y1, n2_4_decoder_1_y2, n2_4_decoder_1_y3;

  _2_4_Decoder u_2_4_decoder_1 (
    .I0(I2), .I1(I3), .EN(EN), .Y0(n2_4_decoder_1_y0), .Y1(n2_4_decoder_1_y1), .Y2(n2_4_decoder_1_y2),
    .Y3(n2_4_decoder_1_y3));
  _2_4_Decoder u_2_4_decoder_2 (.I0(I0), .I1(I1), .EN(n2_4_decoder_1_y0), .Y0(Y0), .Y1(Y1), .Y2(Y2), .Y3(Y3));
  _2_4_Decoder u_2_4_decoder_3 (.I0(I0), .I1(I1), .EN(n2_4_decoder_1_y1), .Y0(Y4), .Y1(Y5), .Y2(Y6), .Y3(Y7));
  _2_4_Decoder u_2_4_decoder_4 (.I0(I0), .I1(I1), .EN(n2_4_decoder_1_y2), .Y0(Y8), .Y1(Y9), .Y2(Y10), .Y3(Y11));
  _2_4_Decoder u_2_4_decoder_5 (.I0(I0), .I1(I1), .EN(n2_4_decoder_1_y3), .Y0(Y12), .Y1(Y13), .Y2(Y14), .Y3(Y15));
endmodule
