// Logisim project Flip-flops.circ as structural Verilog
module Latch_controlado (
  input  S,
  input  R,
  input  C,
  output Q,
  output nQ
);

  wire nand_1_out, nand_2_out;

  nand nand_1 (nand_1_out, S, C);
  nand nand_2 (nand_2_out, R, C);
  nand nand_3 (Q, nand_1_out, nQ);
  nand nand_4 (nQ, Q, nand_2_out);
endmodule

module Latch_tipo_D (
  input  D,
  input  C,
  output Q,
  output nQ
);

  wire nand_1_out, nand_2_out, not_1_out;

  not not_1 (not_1_out, D);
  nand nand_1 (nand_1_out, D, C);
  nand nand_2 (nand_2_out, not_1_out, C);
  nand nand_3 (Q, nand_1_out, nQ);
  nand nand_4 (nQ, Q, nand_2_out);
endmodule

module Flip_flop_mestre_escravo (
  input  S,
  input  R,
  output Q,
  output nQ
);

  wire nand_1_out, nand_2_out, nand_3_out, nand_4_out, nand_5_out, nand_6_out, nC_out, not_1_out;

  Clock nC (.out(nC_out));
  nand nand_1 (nand_1_out, S, nC_out);
  nand nand_2 (nand_2_out, nC_out, R);
  nand nand_3 (nand_3_out, nand_1_out, nand_4_out);
  nand nand_4 (nand_4_out, nand_3_out, nand_2_out);
  not not_1 (not_1_out, nC_out);
  nand nand_5 (nand_5_out, nand_3_out, not_1_out);
  nand nand_6 (nand_6_out, not_1_out, nand_4_out);
  nand nand_7 (Q, nand_5_out, nQ);
  nand nand_8 (nQ, Q, nand_6_out);
endmodule

module \Flip_flop_mestre_escravo_com_entradas_assíncronas  (
  input  nRd,
  input  S,
  input  R,
  input  nSd,
  output Q,
  output nQ
);

  wire and_1_out, and_2_out, nand_1_out, nand_2_out, nand_3_out, nand_4_out, nand_5_out, nand_6_out, nC_out,
       not_1_out;

  Clock nC (.out(nC_out));
  nand nand_1 (nand_1_out, S, nC_out);
  nand nand_2 (nand_2_out, nC_out, R);
  nand nand_3 (nand_3_out, nand_1_out, and_2_out);
  nand nand_4 (nand_4_out, and_1_out, nand_2_out);
  not not_1 (not_1_out, nC_out);
  and and_1 (and_1_out, nRd, nand_3_out);
  and and_2 (and_2_out, nand_4_out, nSd);
  nand nand_5 (nand_5_out, and_1_out, not_1_out);
  nand nand_6 (nand_6_out, not_1_out, and_2_out);
  nand nand_7 (Q, nand_5_out, nSd, nQ);
  nand nand_8 (nQ, Q, nRd, nand_6_out);
endmodule

module Flip_flop_J_K (
  input  J,
  input  K,
  output Q,
  output nQ
);

  wire C_out, nand_1_out, nand_2_out;

  Clock C (.out(C_out));
  nand nand_1 (nand_1_out, J, C_out, nQ);
  nand nand_2 (nand_2_out, Q, C_out, K);
  nand nand_3 (Q, nand_1_out, nQ);
  nand nand_4 (nQ, Q, nand_2_out);
endmodule

module \Contador_assíncrono  (
  output out_1,
  output out_2,
  output out_3,
  output out_4
);

  wire and_1_out, clock_1_out, j_k_ff_1_qn, j_k_ff_2_qn, j_k_ff_3_qn;

  Clock clock_1 (.out(clock_1_out));
  J_K_Flip_Flop j_k_ff_1 (
    .J(1'b1), .clk(clock_1_out), .K(1'b1), .Q(out_1), .Qn(j_k_ff_1_qn), .en(1'b1), .reset(and_1_out));  // open: preset
  J_K_Flip_Flop j_k_ff_2 (
    .J(1'b1), .clk(j_k_ff_1_qn), .K(1'b1), .Q(out_2), .Qn(j_k_ff_2_qn), .en(1'b1), .reset(and_1_out));  // open: preset
  J_K_Flip_Flop j_k_ff_3 (
    .J(1'b1), .clk(j_k_ff_2_qn), .K(1'b1), .Q(out_3), .Qn(j_k_ff_3_qn), .en(1'b1), .reset(and_1_out));  // open: preset
  J_K_Flip_Flop j_k_ff_4 (
    .J(1'b1), .clk(j_k_ff_3_qn), .K(1'b1), .Q(out_4), .en(1'b1), .reset(and_1_out));  // open: Qn, preset
  and and_1 (and_1_out, out_4, out_1);
endmodule

module \Contador_síncrono  (
  output Q0,
  output Q1,
  output Q2,
  output _7,
  output _2,
  output _5
);

  wire and_1_out, clock_1_out, j_k_ff_1_qn, j_k_ff_2_qn, j_k_ff_3_qn;

  Clock clock_1 (.out(clock_1_out));
  J_K_Flip_Flop j_k_ff_1 (.J(1'b1), .clk(clock_1_out), .K(1'b1), .Q(Q0), .Qn(j_k_ff_1_qn));  // open: preset, en, reset
  J_K_Flip_Flop j_k_ff_2 (.J(Q0), .clk(clock_1_out), .K(Q0), .Q(Q1), .Qn(j_k_ff_2_qn));  // open: preset, en, reset
  and and_1 (and_1_out, Q0, Q1);
  J_K_Flip_Flop j_k_ff_3 (
    .J(and_1_out), .clk(clock_1_out), .K(and_1_out), .Q(Q2), .Qn(j_k_ff_3_qn));  // open: preset, en, reset
  and and_2 (_7, Q2, Q1, Q0);
  and and_3 (_2, j_k_ff_3_qn, Q1, j_k_ff_1_qn);
  and and_4 (_5, Q2, j_k_ff_2_qn, Q0);
endmodule

module Contador_crescente_decrescente (
  input  C_D,
  input  En,
  output Q0,
  output Q1,
  output Q2
);

  wire and_1_out, and_2_out, and_3_out, and_4_out, clock_1_out, j_k_ff_1_qn, j_k_ff_2_qn, not_1_out,
       or_1_out, or_2_out;

  Clock clock_1 (.out(clock_1_out));
  J_K_Flip_Flop j_k_ff_1 (
    .J(1'b1), .clk(clock_1_out), .K(1'b1), .Q(Q0), .Qn(j_k_ff_1_qn), .en(En));  // open: preset, reset
  not not_1 (not_1_out, C_D);
  and and_1 (and_1_out, C_D, Q0);
  or or_1 (or_1_out, and_1_out, and_2_out);
  and and_2 (and_2_out, j_k_ff_1_qn, not_1_out);
  J_K_Flip_Flop j_k_ff_2 (
    .J(or_1_out), .clk(clock_1_out), .K(or_1_out), .Q(Q1), .Qn(j_k_ff_2_qn), .en(En));  // open: preset, reset
  and and_3 (and_3_out, and_1_out, Q1);
  or or_2 (or_2_out, and_3_out, and_4_out);
  and and_4 (and_4_out, j_k_ff_2_qn, and_2_out);
  J_K_Flip_Flop j_k_ff_3 (.J(or_2_out), .clk(clock_1_out), .K(or_2_out), .Q(Q2), .en(En));  // open: Qn, preset, reset
endmodule

module \Contador_módulo_10  (
  input  EN,
  output out_2
);

  wire and_1_out, and_2_out, and_3_out, ci_74ls48_1_output_a, ci_74ls48_1_output_b, ci_74ls48_1_output_c,
       ci_74ls48_1_output_d, ci_74ls48_1_output_e, ci_74ls48_1_output_f, ci_74ls48_1_output_g, clock_1_out,
       j_k_ff_1_q, j_k_ff_2_q, j_k_ff_3_q, j_k_ff_4_q;

  Clock clock_1 (.out(clock_1_out));
  CI_74LS48 ci_74ls48_1 (
    .Input_A(j_k_ff_1_q), .Input_B(j_k_ff_2_q), .Input_C(j_k_ff_3_q), .Input_D(j_k_ff_4_q), .BI_RBO(out_2),
    .RBI(1'b1), .LT(1'b1), .Output_a(ci_74ls48_1_output_a), .Output_b(ci_74ls48_1_output_b),
    .Output_c(ci_74ls48_1_output_c), .Output_d(ci_74ls48_1_output_d), .Output_e(ci_74ls48_1_output_e),
    .Output_f(ci_74ls48_1_output_f), .Output_g(ci_74ls48_1_output_g));
  J_K_Flip_Flop j_k_ff_1 (
    .J(1'b1), .clk(clock_1_out), .K(1'b1), .Q(j_k_ff_1_q), .en(EN), .reset(and_1_out));  // open: Qn, preset
  _7_Segment_Display u_7_segment_display_1 (
    .g(ci_74ls48_1_output_g), .f(ci_74ls48_1_output_f), .a(ci_74ls48_1_output_a), .b(ci_74ls48_1_output_b),
    .e(ci_74ls48_1_output_e), .d(ci_74ls48_1_output_d), .c(ci_74ls48_1_output_c));  // open: dp
  J_K_Flip_Flop j_k_ff_2 (
    .J(j_k_ff_1_q), .clk(clock_1_out), .K(j_k_ff_1_q), .Q(j_k_ff_2_q), .en(EN), .reset(and_1_out));  // open: Qn, preset
  and and_1 (and_1_out, j_k_ff_2_q, j_k_ff_4_q);
  and and_2 (and_2_out, j_k_ff_1_q, j_k_ff_2_q);
  J_K_Flip_Flop j_k_ff_3 (
    .J(and_2_out), .clk(clock_1_out), .K(and_2_out), .Q(j_k_ff_3_q), .en(EN), .reset(and_1_out));  // open: Qn, preset
  and and_3 (and_3_out, and_2_out, j_k_ff_3_q);
  J_K_Flip_Flop j_k_ff_4 (
    .J(and_3_out), .clk(clock_1_out), .K(and_3_out), .Q(j_k_ff_4_q), .en(EN), .reset(and_1_out));  // open: Qn, preset
endmodule

module Counters (
  output Q0,
  output Q1,
  output Q2,
  output Q3
);

  wire and_1_out, and_2_out, and_3_out, and_4_out, ci_74ls48_1_output_a, ci_74ls48_1_output_b,
       ci_74ls48_1_output_c, ci_74ls48_1_output_d, ci_74ls48_1_output_e, ci_74ls48_1_output_f,
       ci_74ls48_1_output_g, ci_74ls48_2_output_a, ci_74ls48_2_output_b, ci_74ls48_2_output_c,
       ci_74ls48_2_output_d, ci_74ls48_2_output_e, ci_74ls48_2_output_f, ci_74ls48_2_output_g, clock_1_out,
       clock_2_out, j_k_ff_1_qn, j_k_ff_2_qn, j_k_ff_3_qn, j_k_ff_5_q, j_k_ff_6_q, j_k_ff_7_q, j_k_ff_8_q;

  Clock clock_1 (.out(clock_1_out));
  CI_74LS48 ci_74ls48_1 (
    .Input_A(Q0), .Input_B(Q1), .Input_C(Q2), .Input_D(Q3), .RBI(1'b1), .LT(1'b1),
    .Output_a(ci_74ls48_1_output_a), .Output_b(ci_74ls48_1_output_b), .Output_c(ci_74ls48_1_output_c),
    .Output_d(ci_74ls48_1_output_d), .Output_e(ci_74ls48_1_output_e), .Output_f(ci_74ls48_1_output_f),
    .Output_g(ci_74ls48_1_output_g));  // open: BI_RBO
  J_K_Flip_Flop j_k_ff_1 (
    .J(1'b1), .clk(clock_1_out), .K(1'b1), .Q(Q0), .Qn(j_k_ff_1_qn), .reset(and_1_out));  // open: preset, en
  _7_Segment_Display u_7_segment_display_1 (
    .g(ci_74ls48_1_output_g), .f(ci_74ls48_1_output_f), .a(ci_74ls48_1_output_a), .b(ci_74ls48_1_output_b),
    .e(ci_74ls48_1_output_e), .d(ci_74ls48_1_output_d), .c(ci_74ls48_1_output_c));  // open: dp
  J_K_Flip_Flop j_k_ff_2 (
    .J(1'b1), .clk(j_k_ff_1_qn), .K(1'b1), .Q(Q1), .Qn(j_k_ff_2_qn), .reset(and_1_out));  // open: preset, en
  J_K_Flip_Flop j_k_ff_3 (
    .J(1'b1), .clk(j_k_ff_2_qn), .K(1'b1), .Q(Q2), .Qn(j_k_ff_3_qn), .reset(and_1_out));  // open: preset, en
  J_K_Flip_Flop j_k_ff_4 (.J(1'b1), .clk(j_k_ff_3_qn), .K(1'b1), .Q(Q3), .reset(and_1_out));  // open: Qn, preset, en
  and and_1 (and_1_out, Q1, Q3);
  Clock clock_2 (.out(clock_2_out));
  CI_74LS48 ci_74ls48_2 (
    .Input_A(j_k_ff_5_q), .Input_B(j_k_ff_6_q), .Input_C(j_k_ff_7_q), .Input_D(j_k_ff_8_q), .RBI(1'b1),
    .LT(1'b1), .Output_a(ci_74ls48_2_output_a), .Output_b(ci_74ls48_2_output_b),
    .Output_c(ci_74ls48_2_output_c), .Output_d(ci_74ls48_2_output_d), .Output_e(ci_74ls48_2_output_e),
    .Output_f(ci_74ls48_2_output_f), .Output_g(ci_74ls48_2_output_g));  // open: BI_RBO
  J_K_Flip_Flop j_k_ff_5 (
    .J(1'b1), .clk(clock_2_out), .K(1'b1), .Q(j_k_ff_5_q), .reset(and_4_out));  // open: Qn, preset, en
  _7_Segment_Display u_7_segment_display_2 (
    .g(ci_74ls48_2_output_g), .f(ci_74ls48_2_output_f), .a(ci_74ls48_2_output_a), .b(ci_74ls48_2_output_b),
    .e(ci_74ls48_2_output_e), .d(ci_74ls48_2_output_d), .c(ci_74ls48_2_output_c));  // open: dp
  J_K_Flip_Flop j_k_ff_6 (
    .J(j_k_ff_5_q), .clk(clock_2_out), .K(j_k_ff_5_q), .Q(j_k_ff_6_q), .reset(and_4_out));  // open: Qn, preset, en
  and and_2 (and_2_out, j_k_ff_5_q, j_k_ff_6_q);
  J_K_Flip_Flop j_k_ff_7 (
    .J(and_2_out), .clk(clock_2_out), .K(and_2_out), .Q(j_k_ff_7_q), .reset(and_4_out));  // open: Qn, preset, en
  and and_3 (and_3_out, and_2_out, j_k_ff_7_q);
  J_K_Flip_Flop j_k_ff_8 (
    .J(and_3_out), .clk(clock_2_out), .K(and_3_out), .Q(j_k_ff_8_q), .reset(and_4_out));  // open: Qn, preset, en
  and and_4 (and_4_out, j_k_ff_6_q, j_k_ff_8_q);
endmodule

module Registers (
  input  D,
  input  D_2,
  input  D0,
  input  D1,
  input  D2,
  input  D3,
  input  nLOAD,
  output out_8,
  output out_9,
  output out_10,
  output out_11,
  output out_12,
  output out_13,
  output out_14,
  output out_15,
  output out_16,
  output out_17,
  output out_18,
  output out_19,
  output out_20,
  output out_21,
  output out_22,
  output out_23,
  output out_24,
  output out_25,
  output out_26,
  output out_27
);

  wire and_1_out, and_2_out, and_3_out, and_4_out, and_5_out, and_6_out, and_7_out, clock_1_out, clock_2_out,
       clock_3_out, j_k_ff_1_qn, j_k_ff_2_qn, j_k_ff_3_qn, j_k_ff_4_qn, j_k_ff_5_qn, j_k_ff_6_qn,
       j_k_ff_7_qn, not_1_out, not_2_out, or_1_out, or_2_out, or_3_out;

  Clock clock_1 (.out(clock_1_out));
  Clock clock_2 (.out(clock_2_out));
  J_K_Flip_Flop j_k_ff_1 (
    .J(D), .clk(clock_1_out), .K(not_1_out), .Q(out_8), .Qn(j_k_ff_1_qn));  // open: preset, en, reset
  not not_1 (not_1_out, D);
  D_Flip_Flop d_ff_1 (.clk(clock_2_out), .D(D_2), .Q(out_16));  // open: Qn, preset, en, reset
  not not_2 (not_2_out, nLOAD);
  and and_1 (and_1_out, D0, not_2_out);
  Clock clock_3 (.out(clock_3_out));
  D_Flip_Flop d_ff_2 (.clk(clock_3_out), .D(and_1_out), .Q(out_24));  // open: Qn, preset, en, reset
  J_K_Flip_Flop j_k_ff_2 (
    .J(out_8), .clk(clock_1_out), .K(j_k_ff_1_qn), .Q(out_9), .Qn(j_k_ff_2_qn));  // open: preset, en, reset
  D_Flip_Flop d_ff_3 (.clk(clock_2_out), .D(out_16), .Q(out_17));  // open: Qn, preset, en, reset
  and and_2 (and_2_out, out_24, nLOAD);
  and and_3 (and_3_out, D1, not_2_out);
  or or_1 (or_1_out, and_2_out, and_3_out);
  J_K_Flip_Flop j_k_ff_3 (
    .J(out_9), .clk(clock_1_out), .K(j_k_ff_2_qn), .Q(out_10), .Qn(j_k_ff_3_qn));  // open: preset, en, reset
  D_Flip_Flop d_ff_4 (.clk(clock_2_out), .D(out_17), .Q(out_18));  // open: Qn, preset, en, reset
  D_Flip_Flop d_ff_5 (.clk(clock_3_out), .D(or_1_out), .Q(out_25));  // open: Qn, preset, en, reset
  J_K_Flip_Flop j_k_ff_4 (
    .J(out_10), .clk(clock_1_out), .K(j_k_ff_3_qn), .Q(out_11), .Qn(j_k_ff_4_qn));  // open: preset, en, reset
  D_Flip_Flop d_ff_6 (.clk(clock_2_out), .D(out_18), .Q(out_19));  // open: Qn, preset, en, reset
  and and_4 (and_4_out, out_25, nLOAD);
  and and_5 (and_5_out, D2, not_2_out);
  or or_2 (or_2_out, and_4_out, and_5_out);
  J_K_Flip_Flop j_k_ff_5 (
    .J(out_11), .clk(clock_1_out), .K(j_k_ff_4_qn), .Q(out_12), .Qn(j_k_ff_5_qn));  // open: preset, en, reset
  D_Flip_Flop d_ff_7 (.clk(clock_2_out), .D(out_19), .Q(out_20));  // open: Qn, preset, en, reset
  and and_6 (and_6_out, out_26, nLOAD);
  D_Flip_Flop d_ff_8 (.clk(clock_3_out), .D(or_2_out), .Q(out_26));  // open: Qn, preset, en, reset
  and and_7 (and_7_out, D3, not_2_out);
  or or_3 (or_3_out, and_6_out, and_7_out);
  J_K_Flip_Flop j_k_ff_6 (
    .J(out_12), .clk(clock_1_out), .K(j_k_ff_5_qn), .Q(out_13), .Qn(j_k_ff_6_qn));  // open: preset, en, reset
  D_Flip_Flop d_ff_9 (.clk(clock_2_out), .D(out_20), .Q(out_21));  // open: Qn, preset, en, reset
  D_Flip_Flop d_ff_10 (.clk(clock_3_out), .D(or_3_out), .Q(out_27));  // open: Qn, preset, en, reset
  J_K_Flip_Flop j_k_ff_7 (
    .J(out_13), .clk(clock_1_out), .K(j_k_ff_6_qn), .Q(out_14), .Qn(j_k_ff_7_qn));  // open: preset, en, reset
  D_Flip_Flop d_ff_11 (.clk(clock_2_out), .D(out_21), .Q(out_22));  // open: Qn, preset, en, reset
  J_K_Flip_Flop j_k_ff_8 (.J(out_14), .clk(clock_1_out), .K(j_k_ff_7_qn), .Q(out_15));  // open: Qn, preset, en, reset
  D_Flip_Flop d_ff_12 (.clk(clock_2_out), .D(out_22), .Q(out_23));  // open: Qn, preset, en, reset
endmodule
