// Logisim project P2.circ as structural Verilog: 1 circuit, main circuit main
module main (
  input  A,
  input  A_2,
  input  in_3,
  input  A_3,
  input  A_4,
  input  A_5,
  input  A_6,
  input  in_8,
  input  C,
  input  C_2,
  input  A_7,
  input  A_8,
  input  B,
  input  B_2,
  input  A_9,
  input  A_10,
  input  B_3,
  input  C_3,
  input  B_4,
  input  C_4
);

  wire and_1_out, and_2_out, and_3_out, and_4_out, and_5_out, and_6_out, and_7_out, and_8_out, and_9_out,
       not_1_out, not_2_out, not_3_out, not_4_out, not_5_out, not_6_out, not_7_out, not_8_out, not_9_out,
       or_1_out, or_2_out, or_3_out, or_4_out, or_5_out, or_6_out, or_7_out, or_8_out;

  not not_1 (not_1_out, A_10);
  not not_2 (not_2_out, B_4);
  and and_1 (and_1_out, A, in_3);
  or or_1 (or_1_out, A_4, in_8);
  LED led_1 (.in(and_1_out));
  LED led_2 (.in(or_1_out));
  not not_3 (not_3_out, A_7);
  and and_2 (and_2_out, B_4, not_1_out);
  and and_3 (and_3_out, not_1_out, not_2_out, C_4);
  and and_4 (and_4_out, C, C, A_7);
  and and_5 (and_5_out, not_3_out, B);
  LED led_3 (.in(or_2_out));
  or or_2 (or_2_out, and_4_out, and_5_out);
  or or_3 (or_3_out, and_2_out, and_3_out);
  LED led_4 (.in(not_4_out));
  not not_4 (not_4_out, or_3_out);
  and and_6 (and_6_out, A_2, A_2);
  or or_4 (or_4_out, A_5, A_5);
  LED led_5 (.in(and_6_out));
  LED led_6 (.in(or_4_out));
  not not_5 (not_5_out, A_8);
  or or_5 (or_5_out, C_2, not_5_out);
  or or_6 (or_6_out, A_8, B_2);
  and and_7 (and_7_out, or_5_out, or_6_out);
  not not_6 (not_6_out, B_3);
  not not_7 (not_7_out, C_3);
  not not_8 (not_8_out, A_3);
  not not_9 (not_9_out, A_6);
  LED led_7 (.in(and_7_out));
  and and_8 (and_8_out, not_6_out, not_7_out);
  and and_9 (and_9_out, A_3, not_8_out);
  or or_7 (or_7_out, A_6, not_9_out);
  LED led_8 (.in(and_9_out));
  LED led_9 (.in(or_7_out));
  or or_8 (or_8_out, A_9, and_8_out);
  LED led_10 (.in(or_8_out));

  // Notes on the sheet:
  //   1.4 e 1.5
  //   2.2
  //   1.6
  //   2.5
  //   2.1
  //   1.7
endmodule
