// Logisim project P3.circ as structural Verilog: 1 circuit, main circuit main
module main (
  input  A,
  input  A_2,
  input  B,
  input  B_2,
  input  F,
  input  E,
  input  D,
  input  D_2,
  input  C,
  input  C_2,
  input  B_3,
  input  A_3,
  input  B_4,
  input  A_4,
  input  A_5,
  input  B_5,
  input  A_6,
  input  C_3,
  input  B_6,
  input  D_3,
  input  C_4,
  input  E_2,
  input  D_4,
  input  F_2,
  input  E_3,
  input  G,
  input  H,
  input  I,
  output X,
  output X_2,
  output X_3,
  output Y,
  output X_4,
  output Z,
  output K,
  output W,
  output G1,
  output G2,
  output G3,
  output G1_2,
  output G2_2,
  output G4,
  output G3_2,
  output G5,
  output G4_2,
  output G6,
  output G5_2,
  output G7,
  output G8,
  output G9
);

  wire and_1_out, and_2_out, nand_1_out, nand_2_out, not_1_out, not_2_out, not_3_out, not_4_out, xor_1_out,
       xor_2_out;

  not not_1 (not_1_out, B_2);
  not not_2 (not_2_out, A_2);
  and and_1 (and_1_out, A_2, not_1_out);
  and and_2 (and_2_out, not_2_out, B_2);
  xor xor_1 (xor_1_out, B_3, A_3);
  xor xor_2 (xor_2_out, C, xor_1_out);
  or or_1 (X_2, and_1_out, and_2_out);
  xor xor_3 (X_4, D, xor_2_out);
  xor xor_4 (G2_2, A_6, B_6);
  xor xor_5 (G3_2, B_6, C_4);
  xor xor_6 (G4_2, C_4, D_4);
  xor xor_7 (G5_2, D_4, E_3);
  not not_3 (not_3_out, A);
  not not_4 (not_4_out, B);
  nand nand_1 (nand_1_out, A, B);
  nand nand_2 (nand_2_out, not_3_out, not_4_out);
  xor xor_8 (W, B_4, A_4);
  xor xor_9 (K, C_2, W);
  and and_3 (X, nand_1_out, nand_2_out);
  xor xor_10 (Z, D_2, K);
  xor xor_11 (Y, E, Z);
  xor xor_12 (X_3, F, Y);
  xor xor_13 (G2, A_5, B_5);
  xor xor_14 (G3, B_5, C_3);
  xor xor_15 (G4, C_3, D_3);
  xor xor_16 (G5, D_3, E_2);
  xor xor_17 (G6, E_2, F_2);
  xor xor_18 (G7, F_2, G);
  xor xor_19 (G8, G, H);
  xor xor_20 (G9, H, I);

  assign G1 = A_5;
  assign G1_2 = A_6;

  // Notes on the sheet:
  //   1.1
  //   2.1
  //   3.1
  //   1.2
  //   2.2
  //   3.2
endmodule
