// Logisim project CI 7445.circ as structural Verilog: 2 circuits, main circuit main
module main (
  input  A,
  input  B,
  input  C,
  input  D,
  output _0,
  output _1,
  output _2,
  output _3,
  output _4,
  output _5,
  output _6,
  output _7,
  output _8,
  output _9
);

  CI_7445 ci_7445_1 (
    .Input_A(A), .Input_B(B), .Input_C(C), .Input_D(D), .Output_0(_0), .Output_1(_1), .Output_2(_2),
    .Output_3(_3), .Output_4(_4), .Output_5(_5), .Output_6(_6), .Output_7(_7), .Output_8(_8), .Output_9(_9));

  // Notes on the sheet:
  //   CI 7445
endmodule

module CI_7445 (
  input  Input_A,
  input  Input_B,
  input  Input_C,
  input  Input_D,
  output Output_0,
  output Output_1,
  output Output_2,
  output Output_3,
  output Output_4,
  output Output_5,
  output Output_6,
  output Output_7,
  output Output_8,
  output Output_9
);

  wire not_1_out, not_2_out, not_3_out, not_4_out, not_5_out, not_6_out, not_7_out, not_8_out;

  not not_1 (not_1_out, Input_A);
  not not_2 (not_2_out, Input_B);
  not not_3 (not_3_out, Input_C);
  not not_4 (not_4_out, Input_D);
  not not_5 (not_5_out, not_1_out);
  not not_6 (not_6_out, not_2_out);
  not not_7 (not_7_out, not_3_out);
  not not_8 (not_8_out, not_4_out);
  nand nand_1 (Output_0, not_1_out, not_2_out, not_3_out, not_4_out);
  nand nand_2 (Output_1, not_5_out, not_2_out, not_3_out, not_4_out);
  nand nand_3 (Output_2, not_1_out, not_6_out, not_3_out, not_4_out);
  nand nand_4 (Output_3, not_5_out, not_6_out, not_3_out, not_4_out);
  nand nand_5 (Output_4, not_1_out, not_2_out, not_7_out, not_4_out);
  nand nand_6 (Output_5, not_5_out, not_2_out, not_7_out, not_4_out);
  nand nand_7 (Output_6, not_1_out, not_6_out, not_7_out, not_4_out);
  nand nand_8 (Output_7, not_5_out, not_6_out, not_7_out, not_4_out);
  nand nand_9 (Output_8, not_1_out, not_2_out, not_3_out, not_8_out);
  nand nand_10 (Output_9, not_5_out, not_2_out, not_3_out, not_8_out);
endmodule
