// Logisim project P5.circ as structural Verilog: 8 circuits, main circuit main
module main (
  input  A,
  input  B,
  input  A_2,
  input  B_2,
  input  C,
  output Carry,
  output Sum,
  output Carry_2,
  output Sum_2
);

  Half_Adder half_adder_1 (.A(A), .B(B), .Carry(Carry), .Sum(Sum));
  Full_Adder full_adder_1 (.A(A_2), .B(B_2), .C(C), .Carry(Carry_2), .Sum(Sum_2));
endmodule

module Half_Adder (
  input  A,
  input  B,
  output Carry,
  output Sum
);

  and and_1 (Carry, B, A);
  xor xor_1 (Sum, A, B);
endmodule

module Full_Adder (
  input  A,
  input  B,
  input  C,
  output Carry,
  output Sum
);

  wire half_adder_1_carry, half_adder_1_sum, half_adder_2_carry;

  Half_Adder half_adder_1 (.A(A), .B(B), .Carry(half_adder_1_carry), .Sum(half_adder_1_sum));
  Half_Adder half_adder_2 (.A(half_adder_1_sum), .B(C), .Carry(half_adder_2_carry), .Sum(Sum));
  or or_1 (Carry, half_adder_1_carry, half_adder_2_carry);

  // Notes on the sheet:
  //   Sum
  //   Carry
  //   Carry
endmodule

module Full_Adder__com_portas_discriminadas (
  input  A,
  input  B,
  input  C,
  output C1,
  output Carry,
  output S1,
  output C2,
  output Sum
);

  and and_1 (C1, B, A);
  xor xor_1 (S1, A, B);
  and and_2 (C2, C, S1);
  xor xor_2 (Sum, S1, C);
  or or_1 (Carry, C1, C2);
endmodule

module \Exercício_1  (
  input  A,
  input  B,
  input  C,
  output Carry,
  output Sum
);

  wire and_1_out, and_2_out, and_3_out, and_4_out, and_5_out, and_6_out, and_7_out, not_1_out, not_2_out,
       not_3_out, not_4_out, not_5_out, not_6_out;

  and and_1 (and_1_out, A, B);
  and and_2 (and_2_out, A, C);
  and and_3 (and_3_out, B, C);
  and and_4 (and_4_out, A, B, C);
  not not_1 (not_1_out, A);
  and and_5 (and_5_out, not_1_out, B, not_2_out);
  not not_2 (not_2_out, C);
  and and_6 (and_6_out, A, not_3_out, not_4_out);
  not not_3 (not_3_out, B);
  not not_4 (not_4_out, C);
  not not_5 (not_5_out, A);
  and and_7 (and_7_out, not_5_out, not_6_out, C);
  not not_6 (not_6_out, B);
  or or_1 (Carry, and_1_out, and_2_out, and_3_out);
  or or_2 (Sum, and_4_out, and_5_out, and_6_out, and_7_out);
endmodule

// Ex. 2
module \Exercício_2  (
  input  A0,
  input  B0,
  input  A1,
  input  B1,
  input  A2,
  input  B2,
  input  A3,
  input  B3,
  output S0,
  output S1,
  output S2,
  output S3,
  output Carry
);

  wire full_adder_1_carry, full_adder_2_carry, full_adder_3_carry;

  Full_Adder full_adder_1 (.A(A0), .B(B0), .C(1'b0), .Carry(full_adder_1_carry), .Sum(S0));
  Full_Adder full_adder_2 (.A(A1), .B(B1), .C(full_adder_1_carry), .Carry(full_adder_2_carry), .Sum(S1));
  Full_Adder full_adder_3 (.A(A2), .B(B2), .C(full_adder_2_carry), .Carry(full_adder_3_carry), .Sum(S2));
  Full_Adder full_adder_4 (.A(A3), .B(B3), .C(full_adder_3_carry), .Carry(Carry), .Sum(S3));

  // Notes on the sheet:
  //   Cin
endmodule

module \Exercício_3  (
  input  A3,
  input  A2,
  input  A1,
  input  A0,
  input  B3,
  input  B2,
  input  B1,
  input  B0,
  input  RBI,
  input  LT,
  output out_11,
  output out_12
);

  wire ci_74ls48_1_output_a, ci_74ls48_1_output_b, ci_74ls48_1_output_c, ci_74ls48_1_output_d,
       ci_74ls48_1_output_e, ci_74ls48_1_output_f, ci_74ls48_1_output_g, ci_74ls48_2_output_a,
       ci_74ls48_2_output_b, ci_74ls48_2_output_c, ci_74ls48_2_output_d, ci_74ls48_2_output_e,
       ci_74ls48_2_output_f, ci_74ls48_2_output_g, \exercício_2_1_carry , \exercício_2_1_s0 ,
       \exercício_2_1_s1 , \exercício_2_1_s2 , \exercício_2_1_s3 , n5_bit_to_bcd_1_a1, n5_bit_to_bcd_1_a2,
       n5_bit_to_bcd_1_b1, n5_bit_to_bcd_1_b2, n5_bit_to_bcd_1_c1, n5_bit_to_bcd_1_c2, n5_bit_to_bcd_1_d1,
       n5_bit_to_bcd_1_d2;

  \Exercício_2  \exercício_2_1  (
    .A0(A0), .B0(B0), .A1(A1), .B1(B1), .A2(A2), .B2(B2), .A3(A3), .B3(B3), .S0(\exercício_2_1_s0 ),
    .S1(\exercício_2_1_s1 ), .S2(\exercício_2_1_s2 ), .S3(\exercício_2_1_s3 ), .Carry(\exercício_2_1_carry ));
  _5_bit_to_BCD u_5_bit_to_bcd_1 (
    .E(\exercício_2_1_carry ), .D(\exercício_2_1_s3 ), .C(\exercício_2_1_s2 ), .B(\exercício_2_1_s1 ),
    .A(\exercício_2_1_s0 ), .D2(n5_bit_to_bcd_1_d2), .C2(n5_bit_to_bcd_1_c2), .B2(n5_bit_to_bcd_1_b2),
    .A2(n5_bit_to_bcd_1_a2), .D1(n5_bit_to_bcd_1_d1), .C1(n5_bit_to_bcd_1_c1), .B1(n5_bit_to_bcd_1_b1),
    .A1(n5_bit_to_bcd_1_a1));
  CI_74LS48 ci_74ls48_1 (
    .Input_A(n5_bit_to_bcd_1_a2), .Input_B(n5_bit_to_bcd_1_b2), .Input_C(n5_bit_to_bcd_1_c2),
    .Input_D(n5_bit_to_bcd_1_d2), .BI_RBO(out_11), .RBI(RBI), .LT(LT), .Output_a(ci_74ls48_1_output_a),
    .Output_b(ci_74ls48_1_output_b), .Output_c(ci_74ls48_1_output_c), .Output_d(ci_74ls48_1_output_d),
    .Output_e(ci_74ls48_1_output_e), .Output_f(ci_74ls48_1_output_f), .Output_g(ci_74ls48_1_output_g));
  CI_74LS48 ci_74ls48_2 (
    .Input_A(n5_bit_to_bcd_1_a1), .Input_B(n5_bit_to_bcd_1_b1), .Input_C(n5_bit_to_bcd_1_c1),
    .Input_D(n5_bit_to_bcd_1_d1), .BI_RBO(out_12), .RBI(RBI), .LT(LT), .Output_a(ci_74ls48_2_output_a),
    .Output_b(ci_74ls48_2_output_b), .Output_c(ci_74ls48_2_output_c), .Output_d(ci_74ls48_2_output_d),
    .Output_e(ci_74ls48_2_output_e), .Output_f(ci_74ls48_2_output_f), .Output_g(ci_74ls48_2_output_g));
  _7_Segment_Display u_7_segment_display_1 (
    .g(ci_74ls48_1_output_g), .f(ci_74ls48_1_output_f), .a(ci_74ls48_1_output_a), .b(ci_74ls48_1_output_b),
    .e(ci_74ls48_1_output_e), .d(ci_74ls48_1_output_d), .c(ci_74ls48_1_output_c));  // open: dp
  _7_Segment_Display u_7_segment_display_2 (
    .g(ci_74ls48_2_output_g), .f(ci_74ls48_2_output_f), .a(ci_74ls48_2_output_a), .b(ci_74ls48_2_output_b),
    .e(ci_74ls48_2_output_e), .d(ci_74ls48_2_output_d), .c(ci_74ls48_2_output_c));  // open: dp
endmodule

module _5_bit_to_BCD (
  input  E,
  input  D,
  input  C,
  input  B,
  input  A,
  output D2,
  output C2,
  output B2,
  output A2,
  output D1,
  output C1,
  output B1,
  output A1
);

  wire and_1_out, and_2_out, and_3_out, and_4_out, and_5_out, and_6_out, and_7_out, and_8_out, and_9_out,
       and_10_out, and_11_out, and_12_out, and_13_out, and_14_out, and_15_out, and_16_out, and_17_out,
       and_18_out, not_1_out, not_2_out, not_3_out, not_4_out, not_5_out, not_6_out, not_7_out, not_8_out,
       not_9_out, not_10_out, not_11_out, not_12_out, not_13_out, not_14_out, not_15_out, not_16_out,
       not_17_out, not_18_out, not_19_out, not_20_out, not_21_out, not_22_out, not_23_out, not_24_out,
       not_25_out;

  and and_1 (and_1_out, E, C);
  and and_2 (and_2_out, E, D);
  not not_1 (not_1_out, E);
  not not_2 (not_2_out, E);
  not not_3 (not_3_out, D);
  not not_4 (not_4_out, C);
  not not_5 (not_5_out, E);
  not not_6 (not_6_out, C);
  not not_7 (not_7_out, B);
  not not_8 (not_8_out, D);
  not not_9 (not_9_out, C);
  not not_10 (not_10_out, B);
  not not_11 (not_11_out, E);
  not not_12 (not_12_out, D);
  not not_13 (not_13_out, E);
  not not_14 (not_14_out, C);
  not not_15 (not_15_out, B);
  not not_16 (not_16_out, C);
  not not_17 (not_17_out, E);
  not not_18 (not_18_out, D);
  not not_19 (not_19_out, D);
  not not_20 (not_20_out, E);
  not not_21 (not_21_out, B);
  not not_22 (not_22_out, D);
  not not_23 (not_23_out, C);
  not not_24 (not_24_out, B);
  not not_25 (not_25_out, C);
  or or_1 (B2, and_1_out, and_2_out);
  and and_3 (and_3_out, not_1_out, D, B);
  and and_4 (and_4_out, not_2_out, D, C);
  and and_5 (and_5_out, D, C, B);
  and and_6 (and_6_out, E, not_3_out, not_4_out);
  and and_7 (and_7_out, not_5_out, D, not_6_out, not_7_out);
  and and_8 (and_8_out, E, not_8_out, not_9_out, B);
  and and_9 (and_9_out, E, D, C, not_10_out);
  and and_10 (and_10_out, not_11_out, not_12_out, C);
  and and_11 (and_11_out, not_13_out, C, B);
  and and_12 (and_12_out, E, not_14_out, not_15_out);
  and and_13 (and_13_out, E, D, not_16_out);
  and and_14 (and_14_out, not_17_out, not_18_out, B);
  and and_15 (and_15_out, not_19_out, C, B);
  and and_16 (and_16_out, not_20_out, D, C, not_21_out);
  and and_17 (and_17_out, E, not_22_out, not_23_out, not_24_out);
  and and_18 (and_18_out, E, D, not_25_out, B);
  or or_2 (A2, and_3_out, and_4_out, and_5_out, and_6_out);
  or or_3 (D1, and_7_out, and_8_out, and_9_out);
  or or_4 (C1, and_10_out, and_11_out, and_12_out, and_13_out);
  or or_5 (B1, and_14_out, and_15_out, and_16_out, and_17_out, and_18_out);

  assign A1 = A;
  assign C2 = 1'b0;
  assign D2 = 1'b0;
endmodule
