// Logisim project P6.circ as structural Verilog: 12 circuits, main circuit main
// 74LS139A
module main (
  input  in_1,
  input  in_2,
  input  in_3,
  input  in_4,
  input  in_5,
  input  in_6,
  input  in_7,
  input  in_8,
  input  in_9,
  input  in_10,
  input  in_11,
  input  in_12,
  input  in_13,
  input  in_14,
  input  in_15,
  output out_16,
  output out_17,
  output out_18,
  output out_19,
  output out_20,
  output out_21,
  output out_22,
  output out_23,
  output out_24,
  output out_25,
  output out_26,
  output out_27,
  output out_28
);

  _74LS139A u_74ls139a_1 (
    ._1G(in_1), ._1A(in_2), ._1B(in_3), ._2G(in_4), ._2A(in_5), ._2B(in_6), ._1Y0(out_16), ._1Y1(out_17),
    ._1Y2(out_18), ._1Y3(out_19), ._2Y0(out_20), ._2Y1(out_21), ._2Y2(out_22), ._2Y3(out_23));
  _74LS148 u_74ls148_1 (
    ._0(in_7), ._1(in_8), ._2(in_9), ._3(in_10), ._4(in_11), ._5(in_12), ._6(in_13), ._7(in_14), .nEI(in_15),
    .nEO(out_24), .nGS(out_25), .nA0(out_26), .nA1(out_27), .nA2(out_28));
endmodule

module _74LS139A (
  input  _1G,
  input  _1A,
  input  _1B,
  input  _2G,
  input  _2A,
  input  _2B,
  output _1Y0,
  output _1Y1,
  output _1Y2,
  output _1Y3,
  output _2Y0,
  output _2Y1,
  output _2Y2,
  output _2Y3
);

  wire not_1_out, not_2_out, not_3_out, not_4_out, not_5_out, not_6_out;

  not not_1 (not_1_out, _1G);
  not not_2 (not_2_out, _2G);
  not not_3 (not_3_out, _1A);
  not not_4 (not_4_out, _1B);
  not not_5 (not_5_out, _2A);
  not not_6 (not_6_out, _2B);
  nand nand_1 (_1Y0, not_3_out, not_4_out, not_1_out);
  nand nand_2 (_1Y1, _1A, not_4_out, not_1_out);
  nand nand_3 (_1Y2, _1B, not_3_out, not_1_out);
  nand nand_4 (_1Y3, _1A, _1B, not_1_out);
  nand nand_5 (_2Y0, not_5_out, not_6_out, not_2_out);
  nand nand_6 (_2Y1, _2A, not_6_out, not_2_out);
  nand nand_7 (_2Y2, _2B, not_5_out, not_2_out);
  nand nand_8 (_2Y3, _2A, _2B, not_2_out);
endmodule

module _2_4_Decoder (
  input  _1G,
  input  _1A,
  input  _1B,
  output _1Y0,
  output _1Y1,
  output _1Y2,
  output _1Y3
);

  wire not_1_out, not_2_out, not_3_out;

  not not_1 (not_1_out, _1G);
  not not_2 (not_2_out, _1A);
  not not_3 (not_3_out, _1B);
  nand nand_1 (_1Y0, not_2_out, not_3_out, not_1_out);
  nand nand_2 (_1Y1, _1A, not_3_out, not_1_out);
  nand nand_3 (_1Y2, _1B, not_2_out, not_1_out);
  nand nand_4 (_1Y3, _1A, _1B, not_1_out);
endmodule

module Exercicio_1_4 (
  input  nG,
  input  A,
  input  B,
  input  C,
  output nY0,
  output nY1,
  output nY2,
  output nY3,
  output nY4,
  output nY5,
  output nY6,
  output nY7
);

  wire not_1_out, or_1_out, or_2_out;

  or or_1 (or_1_out, nG, C);
  not not_1 (not_1_out, C);
  or or_2 (or_2_out, nG, not_1_out);
  _2_4_Decoder u_2_4_decoder_1 (._1G(or_1_out), ._1A(A), ._1B(B), ._1Y0(nY0), ._1Y1(nY1), ._1Y2(nY2), ._1Y3(nY3));
  _2_4_Decoder u_2_4_decoder_2 (._1G(or_2_out), ._1A(A), ._1B(B), ._1Y0(nY4), ._1Y1(nY5), ._1Y2(nY6), ._1Y3(nY7));
endmodule

module _74LS148 (
  input  _0,
  input  _1,
  input  _2,
  input  _3,
  input  _4,
  input  _5,
  input  _6,
  input  _7,
  input  nEI,
  output nEO,
  output nGS,
  output nA0,
  output nA1,
  output nA2
);

  wire and_1_out, and_2_out, and_3_out, and_4_out, and_5_out, and_6_out, and_7_out, and_8_out, and_9_out,
       and_10_out, and_11_out, and_12_out, not_1_out, not_2_out, not_3_out, not_4_out, not_5_out, not_6_out,
       not_7_out, not_8_out, not_9_out, not_10_out, not_11_out, not_12_out;

  not not_1 (not_1_out, _1);
  not not_2 (not_2_out, _2);
  not not_3 (not_3_out, _3);
  not not_4 (not_4_out, _4);
  not not_5 (not_5_out, _5);
  not not_6 (not_6_out, _6);
  not not_7 (not_7_out, _7);
  not not_8 (not_8_out, nEI);
  not not_9 (not_9_out, not_2_out);
  not not_10 (not_10_out, not_4_out);
  not not_11 (not_11_out, not_5_out);
  not not_12 (not_12_out, not_6_out);
  nand nand_1 (nEO, _0, _1, _2, _3, _4, _5, _6, _7, not_8_out);
  and and_1 (and_1_out, not_1_out, not_9_out, not_10_out, not_12_out, not_8_out);
  and and_2 (and_2_out, not_3_out, not_10_out, not_12_out, not_8_out);
  and and_3 (and_3_out, not_5_out, not_12_out, not_8_out);
  and and_4 (and_4_out, not_7_out, not_8_out);
  and and_5 (and_5_out, not_2_out, not_10_out, not_11_out, not_8_out);
  and and_6 (and_6_out, not_3_out, not_10_out, not_11_out, not_8_out);
  and and_7 (and_7_out, not_6_out, not_8_out);
  and and_8 (and_8_out, not_7_out, not_8_out);
  and and_9 (and_9_out, not_4_out, not_8_out);
  and and_10 (and_10_out, not_5_out, not_8_out);
  and and_11 (and_11_out, not_6_out, not_8_out);
  and and_12 (and_12_out, not_7_out, not_8_out);
  nand nand_2 (nGS, nEO, not_8_out);
  nor nor_1 (nA0, and_1_out, and_2_out, and_3_out, and_4_out);
  nor nor_2 (nA1, and_5_out, and_6_out, and_7_out, and_8_out);
  nor nor_3 (nA2, and_9_out, and_10_out, and_11_out, and_12_out);
endmodule

module Exercicio_2_2 (
  input  _0,
  input  _1,
  input  _2,
  input  _3,
  input  _4,
  input  _5,
  input  _6,
  input  _7,
  input  _8,
  input  _9,
  input  _10,
  input  _11,
  input  _12,
  input  _13,
  input  _14,
  input  _15,
  input  nEN,
  output _0_2,
  output _1_2,
  output _2_2,
  output _3_2,
  output nPF
);

  wire n74ls148_1_na0, n74ls148_1_na1, n74ls148_1_na2, n74ls148_1_ngs, n74ls148_2_na0, n74ls148_2_na1,
       n74ls148_2_na2, n74ls148_2_neo;

  _74LS148 u_74ls148_1 (
    ._0(_0), ._1(_1), ._2(_2), ._3(_3), ._4(_4), ._5(_5), ._6(_6), ._7(_7), .nEI(n74ls148_2_neo),
    .nGS(n74ls148_1_ngs), .nA0(n74ls148_1_na0), .nA1(n74ls148_1_na1), .nA2(n74ls148_1_na2));  // open: nEO
  _74LS148 u_74ls148_2 (
    ._0(_8), ._1(_9), ._2(_10), ._3(_11), ._4(_12), ._5(_13), ._6(_14), ._7(_15), .nEI(nEN),
    .nEO(n74ls148_2_neo), .nGS(_3_2), .nA0(n74ls148_2_na0), .nA1(n74ls148_2_na1), .nA2(n74ls148_2_na2));
  and and_1 (_0_2, n74ls148_1_na0, n74ls148_2_na0);
  and and_2 (_1_2, n74ls148_1_na1, n74ls148_2_na1);
  and and_3 (_2_2, n74ls148_1_na2, n74ls148_2_na2);
  and and_4 (nPF, n74ls148_1_ngs, _3_2);
endmodule

module _74LS138 (
  input  G1,
  input  G2A,
  input  G2B,
  input  C,
  input  B,
  input  A,
  output Y7,
  output Y6,
  output Y5,
  output Y4,
  output Y3,
  output Y2,
  output Y1,
  output Y0
);

  wire and_1_out, not_1_out, not_2_out, not_3_out, not_4_out, not_5_out;

  not not_1 (not_1_out, G2A);
  and and_1 (and_1_out, G1, not_1_out, not_2_out);
  not not_2 (not_2_out, G2B);
  not not_3 (not_3_out, C);
  not not_4 (not_4_out, B);
  not not_5 (not_5_out, A);
  nand nand_1 (Y7, and_1_out, C, B, A);
  nand nand_2 (Y6, and_1_out, C, B, not_5_out);
  nand nand_3 (Y5, and_1_out, C, not_4_out, A);
  nand nand_4 (Y4, and_1_out, not_5_out, C, not_4_out);
  nand nand_5 (Y3, and_1_out, B, A, not_3_out);
  nand nand_6 (Y2, and_1_out, B, not_3_out, not_5_out);
  nand nand_7 (Y1, and_1_out, not_4_out, not_3_out, A);
  nand nand_8 (Y0, and_1_out, not_5_out, not_4_out, not_3_out);
endmodule

module Exercicio_3_1 (
  input  X2,
  input  X1,
  input  X0,
  output Y
);

  wire n74ls138_1_y0, n74ls138_1_y2, n74ls138_1_y6;

  _74LS138 u_74ls138_1 (
    .G1(1'b1), .G2A(1'b0), .G2B(1'b0), .C(X2), .B(X1), .A(X0), .Y6(n74ls138_1_y6), .Y2(n74ls138_1_y2),
    .Y0(n74ls138_1_y0));  // open: Y7, Y5, Y4, Y3, Y1
  and and_1 (Y, n74ls138_1_y0, n74ls138_1_y2, n74ls138_1_y6);
endmodule

module Exercicio_4_1 (
  input  X2,
  input  X1,
  input  X0,
  output out_4,
  output out_5,
  output nY0,
  output nY1,
  output nY2
);

  wire n74ls138_1_y0, n74ls138_1_y1, n74ls138_1_y2, n74ls138_1_y3, n74ls138_1_y4, n74ls138_1_y5,
       n74ls138_1_y6, n74ls138_1_y7;

  _74LS138 u_74ls138_1 (
    .G1(1'b1), .G2A(1'b0), .G2B(1'b0), .C(X2), .B(X1), .A(X0), .Y7(n74ls138_1_y7), .Y6(n74ls138_1_y6),
    .Y5(n74ls138_1_y5), .Y4(n74ls138_1_y4), .Y3(n74ls138_1_y3), .Y2(n74ls138_1_y2), .Y1(n74ls138_1_y1),
    .Y0(n74ls138_1_y0));
  _74LS148 u_74ls148_1 (
    ._0(n74ls138_1_y0), ._1(n74ls138_1_y1), ._2(n74ls138_1_y3), ._3(n74ls138_1_y2), ._4(n74ls138_1_y7),
    ._5(n74ls138_1_y6), ._6(n74ls138_1_y4), ._7(n74ls138_1_y5), .nEI(1'b0), .nEO(out_4), .nGS(out_5),
    .nA0(nY0), .nA1(nY1), .nA2(nY2));
endmodule

module \Questionário___2  (
  input  EN,
  input  I2,
  input  I3,
  input  I0,
  input  I1,
  output Y0,
  output Y1,
  output Y2,
  output Y3,
  output Y4,
  output Y5,
  output Y6,
  output Y7,
  output Y8,
  output Y9,
  output Y10,
  output Y11,
  output Y12,
  output Y13,
  output Y14,
  output Y15
);

  wire n2_4_decoder_1__1y0, n2_4_decoder_1__1y1, n2_4_decoder_1__1y2, n2_4_decoder_1__1y3;

  _2_4_Decoder u_2_4_decoder_1 (
    ._1G(EN), ._1A(I2), ._1B(I3), ._1Y0(n2_4_decoder_1__1y0), ._1Y1(n2_4_decoder_1__1y1),
    ._1Y2(n2_4_decoder_1__1y2), ._1Y3(n2_4_decoder_1__1y3));
  _2_4_Decoder u_2_4_decoder_2 (
    ._1G(n2_4_decoder_1__1y0), ._1A(I0), ._1B(I1), ._1Y0(Y0), ._1Y1(Y1), ._1Y2(Y2), ._1Y3(Y3));
  _2_4_Decoder u_2_4_decoder_3 (
    ._1G(n2_4_decoder_1__1y1), ._1A(I0), ._1B(I1), ._1Y0(Y4), ._1Y1(Y5), ._1Y2(Y6), ._1Y3(Y7));
  _2_4_Decoder u_2_4_decoder_4 (
    ._1G(n2_4_decoder_1__1y2), ._1A(I0), ._1B(I1), ._1Y0(Y8), ._1Y1(Y9), ._1Y2(Y10), ._1Y3(Y11));
  _2_4_Decoder u_2_4_decoder_5 (
    ._1G(n2_4_decoder_1__1y3), ._1A(I0), ._1B(I1), ._1Y0(Y12), ._1Y1(Y13), ._1Y2(Y14), ._1Y3(Y15));
endmodule

module _3_8_Decoder (
  input  EN,
  input  C,
  input  B,
  input  A,
  output Y7,
  output Y6,
  output Y5,
  output Y4,
  output Y3,
  output Y2,
  output Y1,
  output Y0
);

  wire not_1_out, not_2_out, not_3_out;

  not not_1 (not_1_out, C);
  not not_2 (not_2_out, B);
  not not_3 (not_3_out, A);
  and and_1 (Y7, EN, C, B, A);
  and and_2 (Y6, EN, C, B, not_3_out);
  and and_3 (Y5, EN, C, not_2_out, A);
  and and_4 (Y4, EN, not_3_out, C, not_2_out);
  and and_5 (Y3, EN, B, A, not_1_out);
  and and_6 (Y2, EN, B, not_1_out, not_3_out);
  and and_7 (Y1, EN, not_2_out, not_1_out, A);
  and and_8 (Y0, EN, not_3_out, not_2_out, not_1_out);
endmodule

module \Questionário___3  (
  input  EN,
  input  X2,
  input  X1,
  input  X0,
  output Y
);

  wire n3_8_decoder_1_y1, n3_8_decoder_1_y2, n3_8_decoder_1_y4, n3_8_decoder_1_y7;

  _3_8_Decoder u_3_8_decoder_1 (
    .EN(EN), .C(X2), .B(X1), .A(X0), .Y7(n3_8_decoder_1_y7), .Y4(n3_8_decoder_1_y4), .Y2(n3_8_decoder_1_y2),
    .Y1(n3_8_decoder_1_y1));  // open: Y6, Y5, Y3, Y0
  or or_1 (Y, n3_8_decoder_1_y1, n3_8_decoder_1_y2, n3_8_decoder_1_y4, n3_8_decoder_1_y7);
endmodule
