// Logisim project P7.circ as structural Verilog
module _74LS153 (
  input  nG1,
  input  _1C0,
  input  _1C1,
  input  _1C2,
  input  _1C3,
  input  B,
  input  A,
  input  _2C0,
  input  _2C1,
  input  _2C2,
  input  _2C3,
  input  nG2,
  output Y1,
  output Y2
);

  wire and_1_out, and_2_out, and_3_out, and_4_out, and_5_out, and_6_out, and_7_out, and_8_out, not_1_out,
       not_2_out, not_3_out, not_4_out, not_5_out, not_6_out;

  not not_1 (not_1_out, B);
  not not_2 (not_2_out, A);
  not not_3 (not_3_out, nG1);
  not not_4 (not_4_out, not_1_out);
  not not_5 (not_5_out, not_2_out);
  not not_6 (not_6_out, nG2);
  and and_1 (and_1_out, not_3_out, not_1_out, not_2_out, _1C0);
  and and_2 (and_2_out, not_3_out, not_1_out, not_5_out, _1C1);
  and and_3 (and_3_out, not_3_out, not_4_out, not_2_out, _1C2);
  and and_4 (and_4_out, not_3_out, not_4_out, not_5_out, _1C3);
  and and_5 (and_5_out, _2C0, not_1_out, not_2_out, not_6_out);
  and and_6 (and_6_out, _2C1, not_1_out, not_5_out, not_6_out);
  and and_7 (and_7_out, _2C2, not_4_out, not_2_out, not_6_out);
  and and_8 (and_8_out, _2C3, not_4_out, not_5_out, not_6_out);
  or or_1 (Y1, and_1_out, and_2_out, and_3_out, and_4_out);
  or or_2 (Y2, and_5_out, and_6_out, and_7_out, and_8_out);
endmodule

module Ex__1_1 (
  input  nG,
  input  B,
  input  A,
  output Y
);

  wire clock_1_out;

  Clock clock_1 (.out(clock_1_out));
  _74LS153 u_74ls153_1 (
    .nG1(nG), ._1C1(clock_1_out), ._1C2(1'b0), ._1C3(1'b1), .B(B), .A(A), .Y1(Y));  // open: _1C0, _2C0, _2C1, _2C2, _2C3, nG2, Y2
endmodule

module _74LS157 (
  input  A1,
  input  B1,
  input  A2,
  input  B2,
  input  A3,
  input  B3,
  input  A4,
  input  B4,
  input  Select,
  input  Strobe,
  output Y1,
  output Y2,
  output Y3,
  output Y4
);

  wire and_1_out, and_2_out, and_3_out, and_4_out, and_5_out, and_6_out, and_7_out, and_8_out, not_1_out,
       not_2_out, not_3_out;

  not not_1 (not_1_out, Select);
  not not_2 (not_2_out, Strobe);
  not not_3 (not_3_out, not_1_out);
  and and_1 (and_1_out, A1, not_1_out, not_2_out);
  and and_2 (and_2_out, B1, not_3_out, not_2_out);
  and and_3 (and_3_out, A2, not_1_out, not_2_out);
  and and_4 (and_4_out, B2, not_3_out, not_2_out);
  and and_5 (and_5_out, A3, not_1_out, not_2_out);
  and and_6 (and_6_out, B3, not_3_out, not_2_out);
  and and_7 (and_7_out, A4, not_1_out, not_2_out);
  and and_8 (and_8_out, B4, not_3_out, not_2_out);
  or or_1 (Y1, and_1_out, and_2_out);
  or or_2 (Y2, and_3_out, and_4_out);
  or or_3 (Y3, and_5_out, and_6_out);
  or or_4 (Y4, and_7_out, and_8_out);
endmodule

module Ex__1_2 (
  input  S0,
  input  S1,
  input  S0_2,
  input  EN,
  input  S1_2,
  input  nG,
  output Y0,
  output Y1,
  output Y,
  output Y_2
);

  wire multiplexer_1_out, multiplexer_2_out, X1_2_out, X1_out;

  Clock X1 (.out(X1_out));
  _74LS157 u_74ls157_1 (
    .B1(X1_out), .A2(1'b0), .B2(1'b1), .Select(S0), .Strobe(nG), .Y1(Y0), .Y2(Y1));  // open: A1, A3, B3, A4, B4, Y3, Y4
  _74LS157 u_74ls157_2 (
    .A1(Y0), .B1(Y1), .Select(S1), .Strobe(nG), .Y1(Y));  // open: A2, B2, A3, B3, A4, B4, Y2, Y3, Y4
  Clock X1_2 (.out(X1_2_out));
  Multiplexer multiplexer_1 (.in1(X1_2_out), .out(multiplexer_1_out), .sel(S0_2), .en(EN));  // open: in0
  Multiplexer multiplexer_2 (.in0(1'b0), .in1(1'b1), .out(multiplexer_2_out), .sel(S0_2), .en(EN));
  Multiplexer multiplexer_3 (.in0(multiplexer_1_out), .in1(multiplexer_2_out), .out(Y_2), .sel(S1_2), .en(EN));

  // Notes on the sheet:
  //   X2
  //   X3
  //   X0
  //   X2
  //   X3
endmodule

module Ex__2_1 (
  input  A,
  input  B,
  output out_3,
  output out_4,
  output out_5,
  output out_6
);

  wire nG_out;

  Clock nG (.out(nG_out));
  _74LS139A u_74ls139a_1 (
    ._1G(nG_out), ._1A(A), ._1B(B), ._1Y0(out_3), ._1Y1(out_4), ._1Y2(out_5), ._1Y3(out_6));  // open: _2G, _2A, _2B, _2Y0, _2Y1, _2Y2, _2Y3
endmodule

module _74LS151 (
  input  Y7,
  input  Y6,
  input  Y5,
  input  Y4,
  input  Y3,
  input  Y2,
  input  Y1,
  input  Y0,
  input  C,
  input  B,
  input  A,
  input  nEN,
  output Y,
  output W
);

  wire and_1_out, and_2_out, and_3_out, and_4_out, and_5_out, and_6_out, and_7_out, and_8_out, not_1_out,
       not_2_out, not_3_out, not_4_out;

  not not_1 (not_1_out, nEN);
  not not_2 (not_2_out, C);
  not not_3 (not_3_out, B);
  not not_4 (not_4_out, A);
  and and_1 (and_1_out, Y7, C, B, A, not_1_out);
  and and_2 (and_2_out, Y6, C, B, not_4_out, not_1_out);
  and and_3 (and_3_out, Y5, C, not_3_out, A, not_1_out);
  and and_4 (and_4_out, Y4, C, not_3_out, not_4_out, not_1_out);
  and and_5 (and_5_out, Y3, not_2_out, B, A, not_1_out);
  and and_6 (and_6_out, Y2, not_2_out, B, not_4_out, not_1_out);
  and and_7 (and_7_out, Y1, not_2_out, not_3_out, A, not_1_out);
  and and_8 (and_8_out, Y0, not_2_out, not_3_out, not_4_out, not_1_out);
  nor nor_1 (W, and_1_out, and_2_out, and_3_out, and_4_out, and_5_out, and_6_out, and_7_out, and_8_out);
  not not_5 (Y, W);
endmodule

module Ex__3_1 (
  input  X2,
  input  X1,
  input  X0,
  output Y
);

  _74LS151 u_74ls151_1 (
    .Y7(1'b1), .Y6(1'b0), .Y5(1'b1), .Y4(1'b1), .Y3(1'b0), .Y2(1'b1), .Y1(1'b0), .Y0(1'b0), .C(X2), .B(X1),
    .A(X0), .nEN(1'b0), .Y(Y));  // open: W
endmodule

module Ex__3_4 (
  input  X0,
  input  X2,
  input  X1,
  output Y
);

  wire not_1_out;

  not not_1 (not_1_out, X0);
  _74LS153 u_74ls153_1 (
    .nG1(1'b0), ._1C0(1'b0), ._1C1(not_1_out), ._1C2(1'b1), ._1C3(X0), .B(X2), .A(X1), .Y1(Y));  // open: _2C0, _2C1, _2C2, _2C3, nG2, Y2
endmodule

module MUX_4_1 (
  input  I3,
  input  I2,
  input  I1,
  input  I0,
  input  B,
  input  A,
  input  nEN,
  output out_8
);

  wire and_1_out, and_2_out, and_3_out, and_4_out, not_1_out, not_2_out, not_3_out;

  not not_1 (not_1_out, B);
  not not_2 (not_2_out, A);
  not not_3 (not_3_out, nEN);
  and and_1 (and_1_out, I3, B, A, not_3_out);
  and and_2 (and_2_out, I2, B, not_2_out, not_3_out);
  and and_3 (and_3_out, I1, not_1_out, A, not_3_out);
  and and_4 (and_4_out, I0, not_1_out, not_2_out, not_3_out);
  or or_1 (out_8, and_1_out, and_2_out, and_3_out, and_4_out);
endmodule

module \Questionário_1  (
  input  X15,
  input  X14,
  input  nEN,
  input  X13,
  input  X12,
  input  X11,
  input  X10,
  input  X9,
  input  X8,
  input  X7,
  input  X6,
  input  X5,
  input  X4,
  input  X3,
  input  X2,
  input  X1,
  input  X0,
  input  S2,
  input  S3,
  input  S0,
  input  S1,
  output Y
);

  wire mux_4_1_1_out_8, mux_4_1_2_out_8, mux_4_1_3_out_8, mux_4_1_4_out_8;

  MUX_4_1 mux_4_1_1 (.I3(X15), .I2(X14), .I1(X13), .I0(X12), .B(S1), .A(S0), .nEN(nEN), .out_8(mux_4_1_1_out_8));
  MUX_4_1 mux_4_1_2 (.I3(X11), .I2(X10), .I1(X9), .I0(X8), .B(S1), .A(S0), .nEN(nEN), .out_8(mux_4_1_2_out_8));
  MUX_4_1 mux_4_1_3 (.I3(X7), .I2(X6), .I1(X5), .I0(X4), .B(S1), .A(S0), .nEN(nEN), .out_8(mux_4_1_3_out_8));
  MUX_4_1 mux_4_1_4 (.I3(X3), .I2(X2), .I1(X1), .I0(X0), .B(S1), .A(S0), .nEN(nEN), .out_8(mux_4_1_4_out_8));
  MUX_4_1 mux_4_1_5 (
    .I3(mux_4_1_1_out_8), .I2(mux_4_1_2_out_8), .I1(mux_4_1_3_out_8), .I0(mux_4_1_4_out_8), .B(S3), .A(S2),
    .nEN(nEN), .out_8(Y));
endmodule

module \Questionário_2  (
  input  EN,
  input  D0,
  input  D1,
  input  D2,
  input  D3,
  input  D4,
  input  D5,
  input  D6,
  input  D7,
  input  S0,
  input  S1,
  input  S2,
  output Y
);

  wire multiplexer_1_out, multiplexer_2_out, multiplexer_3_out, multiplexer_4_out, multiplexer_5_out,
       multiplexer_6_out;

  Multiplexer multiplexer_1 (.in0(D0), .in1(D1), .out(multiplexer_1_out), .sel(S0), .en(EN));
  Multiplexer multiplexer_2 (.in0(D2), .in1(D3), .out(multiplexer_2_out), .sel(S0), .en(EN));
  Multiplexer multiplexer_3 (.in0(D4), .in1(D5), .out(multiplexer_3_out), .sel(S0), .en(EN));
  Multiplexer multiplexer_4 (.in0(D6), .in1(D7), .out(multiplexer_4_out), .sel(S0), .en(EN));
  Multiplexer multiplexer_5 (
    .in0(multiplexer_1_out), .in1(multiplexer_2_out), .out(multiplexer_5_out), .sel(S1), .en(EN));
  Multiplexer multiplexer_6 (
    .in0(multiplexer_3_out), .in1(multiplexer_4_out), .out(multiplexer_6_out), .sel(S1), .en(EN));
  Multiplexer multiplexer_7 (.in0(multiplexer_5_out), .in1(multiplexer_6_out), .out(Y), .sel(S2), .en(EN));
endmodule

module \Questionário_3  (
  input  X3,
  input  X2,
  input  X1,
  input  X0,
  input  nEN,
  output Y
);

  wire not_1_out;

  not not_1 (not_1_out, X3);
  _74LS151 MUX_8_1 (
    .Y7(not_1_out), .Y6(X3), .Y5(1'b0), .Y4(not_1_out), .Y3(1'b1), .Y2(1'b0), .Y1(not_1_out), .Y0(not_1_out),
    .C(X2), .B(X1), .A(X0), .nEN(nEN), .Y(Y));  // open: W
endmodule
