// Logisim project P8.circ as structural Verilog: 9 circuits, main circuit main
module main (
  input  T,
  input  Sd,
  input  Cd,
  output out_4,
  output out_5
);

  wire not_1_out;

  J_K_Flip_Flop #(.trigger("falling")) j_k_ff_1 (
    .J(1'b1), .clk(T), .K(1'b1), .Q(out_4), .Qn(out_5), .preset(not_1_out), .en(1'b1), .reset(Cd));
  not not_1 (not_1_out, Sd);
endmodule

module _1_1_1 (
  input  nS,
  input  nR,
  output Q,
  output nQ
);

  nand nand_1 (Q, nS, nQ);
  nand nand_2 (nQ, Q, nR);
endmodule

module _1_1_3 (
  input  R,
  input  S,
  output Q,
  output nQ
);

  nor nor_1 (Q, R, nQ);
  nor nor_2 (nQ, Q, S);
endmodule

module _1_2_1 (
  input  S,
  input  R,
  output Q,
  output nQ
);

  wire nand_1_out, nand_2_out, Shift_out;

  Clock Shift (.out(Shift_out));
  nand nand_1 (nand_1_out, S, Shift_out);
  nand nand_2 (nand_2_out, Shift_out, R);
  nand nand_3 (Q, nand_1_out, nQ);
  nand nand_4 (nQ, Q, nand_2_out);
endmodule

module _74LS76A (
  input  nPRE,
  input  nCLR,
  input  K,
  input  J,
  input  CLK,
  output Q,
  output nQ
);

  wire and_1_out, and_2_out, and_3_out, and_4_out, nand_1_out, nand_2_out;

  nor nor_1 (Q, and_1_out, and_2_out);
  and and_1 (and_1_out, nQ, nand_2_out, nPRE);
  and and_2 (and_2_out, nQ, CLK, nPRE);
  nand nand_1 (nand_1_out, nPRE, Q, K, CLK);
  nand nand_2 (nand_2_out, nCLR, nQ, J, CLK);
  and and_3 (and_3_out, Q, nand_1_out, nCLR);
  and and_4 (and_4_out, Q, CLK, nCLR);
  nor nor_2 (nQ, and_3_out, and_4_out);
endmodule

module _1_3_1 (
  input  J,
  input  J_2,
  input  K,
  input  K_2,
  input  in_5,
  input  in_6,
  output Q,
  output Q_2,
  output nQ,
  output nQ_2
);

  wire and_1_out, and_2_out, and_3_out, and_4_out, CLK_2_out, CLK_out, not_1_out, not_2_out, not_3_out;

  Clock CLK (.out(CLK_out));
  and and_1 (and_1_out, J_2, CLK_out);
  not not_1 (not_1_out, CLK_out);
  and and_2 (and_2_out, CLK_out, K_2);
  _74LS76A u_74ls76a_1 (.Q(Q), .nPRE(1'b1), .K(and_2_out), .nQ(nQ_2), .nCLR(1'b1), .J(and_1_out), .CLK(not_1_out));
  Clock CLK_2 (.out(CLK_2_out));
  and and_3 (and_3_out, J, CLK_2_out);
  J_K_Flip_Flop #(.trigger("falling")) j_k_ff_1 (
    .J(and_3_out), .clk(CLK_2_out), .K(and_4_out), .Q(Q_2), .Qn(nQ), .preset(not_2_out), .en(1'b1),
    .reset(not_3_out));
  and and_4 (and_4_out, CLK_2_out, K);
  not not_2 (not_2_out, in_5);
  not not_3 (not_3_out, in_6);
endmodule

module _1_3_3 (
  input  T,
  input  Sd,
  input  Cd,
  output out_4,
  output out_5
);

  wire not_1_out;

  J_K_Flip_Flop j_k_ff_1 (
    .J(1'b1), .clk(T), .K(1'b1), .Q(out_4), .Qn(out_5), .preset(not_1_out), .en(1'b1), .reset(Cd));
  not not_1 (not_1_out, Sd);
endmodule

module _74LS193 (
  input  A,
  input  B,
  input  C,
  input  D,
  input  nLOAD,
  input  UP,
  input  DOWN,
  input  CLEAR,
  output nCO,
  output nBO,
  output QA,
  output QB,
  output QC,
  output QD
);

  wire and_1_out, and_2_out, and_3_out, and_4_out, and_5_out, and_6_out, n1_3_3_1_out_5, n1_3_3_2_out_5,
       n1_3_3_3_out_5, n1_3_3_4_out_5, nand_1_out, nand_2_out, nand_3_out, nand_4_out, nand_5_out,
       nand_6_out, nand_7_out, nand_8_out, nand_9_out, nand_10_out, nand_11_out, nand_12_out, nor_1_out,
       nor_2_out, nor_3_out, nor_4_out, not_1_out, not_2_out, not_3_out, not_4_out;

  not not_1 (not_1_out, nLOAD);
  not not_2 (not_2_out, UP);
  not not_3 (not_3_out, DOWN);
  not not_4 (not_4_out, CLEAR);
  nand nand_1 (nand_1_out, not_1_out, not_4_out, A);
  nor nor_1 (nor_1_out, not_2_out, not_3_out);
  nand nand_2 (nand_2_out, nand_1_out, not_1_out);
  _1_3_3 u_1_3_3_1 (.T(nor_1_out), .out_4(QA), .out_5(n1_3_3_1_out_5), .Sd(nand_1_out), .Cd(nand_3_out));
  nand nand_3 (nand_3_out, not_4_out, nand_2_out);
  and and_1 (and_1_out, not_4_out, QA);
  and and_2 (and_2_out, n1_3_3_1_out_5, not_3_out);
  nand nand_4 (nand_4_out, not_1_out, not_4_out, B);
  nor nor_2 (nor_2_out, and_1_out, and_2_out);
  nand nand_5 (nand_5_out, not_4_out, nand_6_out);
  nand nand_6 (nand_6_out, nand_4_out, not_1_out);
  _1_3_3 u_1_3_3_2 (.T(nor_2_out), .out_4(QB), .out_5(n1_3_3_2_out_5), .Sd(nand_4_out), .Cd(nand_5_out));
  and and_3 (and_3_out, not_4_out, QA, QB);
  and and_4 (and_4_out, n1_3_3_2_out_5, n1_3_3_1_out_5, not_3_out);
  nand nand_7 (nand_7_out, not_1_out, not_4_out, C);
  _1_3_3 u_1_3_3_3 (.T(nor_3_out), .out_4(QC), .out_5(n1_3_3_3_out_5), .Sd(nand_7_out), .Cd(nand_8_out));
  nor nor_3 (nor_3_out, and_3_out, and_4_out);
  nand nand_8 (nand_8_out, not_4_out, nand_9_out);
  nand nand_9 (nand_9_out, nand_7_out, not_1_out);
  nand nand_10 (nand_10_out, not_1_out, not_4_out, D);
  and and_5 (and_5_out, not_4_out, QA, QB, QC);
  nor nor_4 (nor_4_out, and_5_out, and_6_out);
  and and_6 (and_6_out, n1_3_3_3_out_5, n1_3_3_1_out_5, n1_3_3_2_out_5, not_3_out);
  nand nand_11 (nand_11_out, nand_10_out, not_1_out);
  _1_3_3 u_1_3_3_4 (.T(nor_4_out), .out_4(QD), .out_5(n1_3_3_4_out_5), .Sd(nand_10_out), .Cd(nand_12_out));
  nand nand_12 (nand_12_out, not_4_out, nand_11_out);
  nand nand_13 (nCO, not_4_out, QA, QB, QC, QD);
  nand nand_14 (nBO, n1_3_3_4_out_5, n1_3_3_3_out_5, n1_3_3_1_out_5, n1_3_3_2_out_5, not_3_out);
endmodule

module _2_4 (
  output out_1,
  output out_2
);

  wire ci_74ls48_1_output_a, ci_74ls48_1_output_b, ci_74ls48_1_output_c, ci_74ls48_1_output_d,
       ci_74ls48_1_output_e, ci_74ls48_1_output_f, ci_74ls48_1_output_g, ci_74ls48_2_output_a,
       ci_74ls48_2_output_b, ci_74ls48_2_output_c, ci_74ls48_2_output_d, ci_74ls48_2_output_e,
       ci_74ls48_2_output_f, ci_74ls48_2_output_g, clock_1_out, n5_bit_to_bcd_1_a1, n5_bit_to_bcd_1_a2,
       n5_bit_to_bcd_1_b1, n5_bit_to_bcd_1_b2, n5_bit_to_bcd_1_c1, n5_bit_to_bcd_1_c2, n5_bit_to_bcd_1_d1,
       n5_bit_to_bcd_1_d2, n74ls193_1_qa, n74ls193_1_qb, n74ls193_1_qc, n74ls193_1_qd, nand_1_out;

  Clock clock_1 (.out(clock_1_out));
  nand nand_1 (nand_1_out, n74ls193_1_qd, n74ls193_1_qc, n74ls193_1_qb, n74ls193_1_qa);
  _74LS193 u_74ls193_1 (
    .nLOAD(nand_1_out), .UP(clock_1_out), .DOWN(1'b1), .CLEAR(1'b0), .A(1'b0), .B(1'b1), .C(1'b1), .D(1'b0),
    .QA(n74ls193_1_qa), .QB(n74ls193_1_qb), .QC(n74ls193_1_qc), .QD(n74ls193_1_qd));  // open: nCO, nBO
  _5_bit_to_BCD u_5_bit_to_bcd_1 (
    .E(1'b0), .D(n74ls193_1_qd), .C(n74ls193_1_qc), .B(n74ls193_1_qb), .A(n74ls193_1_qa),
    .D2(n5_bit_to_bcd_1_d2), .C2(n5_bit_to_bcd_1_c2), .B2(n5_bit_to_bcd_1_b2), .A2(n5_bit_to_bcd_1_a2),
    .D1(n5_bit_to_bcd_1_d1), .C1(n5_bit_to_bcd_1_c1), .B1(n5_bit_to_bcd_1_b1), .A1(n5_bit_to_bcd_1_a1));
  CI_74LS48 ci_74ls48_1 (
    .Input_A(n5_bit_to_bcd_1_a2), .Input_B(n5_bit_to_bcd_1_b2), .Input_C(n5_bit_to_bcd_1_c2),
    .Input_D(n5_bit_to_bcd_1_d2), .BI_RBO(out_1), .RBI(1'b1), .LT(1'b1), .Output_a(ci_74ls48_1_output_a),
    .Output_b(ci_74ls48_1_output_b), .Output_c(ci_74ls48_1_output_c), .Output_d(ci_74ls48_1_output_d),
    .Output_e(ci_74ls48_1_output_e), .Output_f(ci_74ls48_1_output_f), .Output_g(ci_74ls48_1_output_g));
  CI_74LS48 ci_74ls48_2 (
    .Input_A(n5_bit_to_bcd_1_a1), .Input_B(n5_bit_to_bcd_1_b1), .Input_C(n5_bit_to_bcd_1_c1),
    .Input_D(n5_bit_to_bcd_1_d1), .BI_RBO(out_2), .RBI(1'b1), .LT(1'b1), .Output_a(ci_74ls48_2_output_a),
    .Output_b(ci_74ls48_2_output_b), .Output_c(ci_74ls48_2_output_c), .Output_d(ci_74ls48_2_output_d),
    .Output_e(ci_74ls48_2_output_e), .Output_f(ci_74ls48_2_output_f), .Output_g(ci_74ls48_2_output_g));
  _7_Segment_Display u_7_segment_display_1 (
    .g(ci_74ls48_1_output_g), .f(ci_74ls48_1_output_f), .a(ci_74ls48_1_output_a), .b(ci_74ls48_1_output_b),
    .e(ci_74ls48_1_output_e), .d(ci_74ls48_1_output_d), .c(ci_74ls48_1_output_c));  // open: dp
  _7_Segment_Display u_7_segment_display_2 (
    .g(ci_74ls48_2_output_g), .f(ci_74ls48_2_output_f), .a(ci_74ls48_2_output_a), .b(ci_74ls48_2_output_b),
    .e(ci_74ls48_2_output_e), .d(ci_74ls48_2_output_d), .c(ci_74ls48_2_output_c));  // open: dp
endmodule
